# Fritzing sketch hardware_sketch (saved by Fritzing 0.9.4)

parts:
  M1 = ESP32-C3-DevKitM-1 [part_number="M5Stamp C3U"]
  IC1 = Voltage Regulator [package=78xxl]
  V1 = DC Power [voltage=12V]
  V2 = AC Power [voltage=12V frequency=50]
  R1 = Resistor [tolerance=±5% resistance=2.2k package=THT]
  D1 = Diode [part_number=1N4148 package=diode-1n4148]
  U1 = Optocoupler [part_number=H11L1 package=THT]

nets:
  N1: M1.3, U1.Pin_4
  N2: M1.GND-27, M1.GND-30, IC1.GND, V1.V-, V2.V-, D1.A, U1.Pin_2
  N3: M1.5V-28, M1.5V-29, IC1.OUT
  N4: IC1.IN, V1.V+
  N5: V2.V+, R1.Pin_0
  N6: R1.Pin_1, D1.C, U1.Pin_1

custom parts:
  ESP32-C3-DevKitM-1: Espressif Esp32 DevKit v1 is one of the development board created by DOIT to evaluate the ESP-WROOM-32 module. It is based on the ESP32 microcontroller that boasts Wifi, Bluetooth, Ethernet and Low Power support all in a single chip. (vanepp) Feb 2021: converted to ESP32-C3-DevKitM-1. This chip is 30pins long (2 x15) and 11 pins width.
